// Logisim project 8bitadder.circ as structural Verilog: 1 circuit, main circuit main
module main (
);

  wire and_1_out, and_2_out, and_3_out, and_4_out, and_5_out, and_6_out, and_7_out, and_8_out, and_9_out,
       and_10_out, and_11_out, and_12_out, and_13_out, and_14_out, and_15_out, and_16_out, and_17_out,
       and_18_out, and_19_out, and_20_out, and_21_out, and_22_out, and_23_out, and_24_out, or_1_out,
       or_2_out, or_3_out, or_4_out, or_5_out, or_6_out, or_7_out, or_8_out;
  wire [7:0] xor_1_out;

  // Probe on or_8_out
  and and_1 (and_1_out, 1'b0, 1'b1);
  and and_2 (and_2_out, 1'b0, 1'b0);
  and and_3 (and_3_out, 1'b1, 1'b0);
  ExactlyOne xor_1 (.out(xor_1_out[0]), .in0(1'b0), .in2(1'b1), .in4(1'b0));
  and and_4 (and_4_out, or_1_out, 1'b0);
  and and_5 (and_5_out, or_1_out, 1'b0);
  and and_6 (and_6_out, 1'b0, 1'b0);
  ExactlyOne xor_2 (.out(xor_1_out[1]), .in0(or_1_out), .in2(1'b0), .in4(1'b0));
  and and_7 (and_7_out, or_2_out, 1'b1);
  and and_8 (and_8_out, or_2_out, 1'b0);
  and and_9 (and_9_out, 1'b1, 1'b0);
  ExactlyOne xor_3 (.out(xor_1_out[2]), .in0(or_2_out), .in2(1'b1), .in4(1'b0));
  and and_10 (and_10_out, or_3_out, 1'b0);
  and and_11 (and_11_out, or_3_out, 1'b0);
  and and_12 (and_12_out, 1'b0, 1'b0);
  ExactlyOne xor_4 (.out(xor_1_out[3]), .in0(or_3_out), .in2(1'b0), .in4(1'b0));
  and and_13 (and_13_out, or_4_out, 1'b1);
  and and_14 (and_14_out, or_4_out, 1'b0);
  and and_15 (and_15_out, 1'b1, 1'b0);
  ExactlyOne xor_5 (.out(xor_1_out[4]), .in0(or_4_out), .in2(1'b1), .in4(1'b0));
  and and_16 (and_16_out, or_5_out, 1'b0);
  and and_17 (and_17_out, or_5_out, 1'b1);
  and and_18 (and_18_out, 1'b0, 1'b1);
  ExactlyOne xor_6 (.out(xor_1_out[5]), .in0(or_5_out), .in2(1'b0), .in4(1'b1));
  and and_19 (and_19_out, or_6_out, 1'b1);
  and and_20 (and_20_out, or_6_out, 1'b0);
  and and_21 (and_21_out, 1'b1, 1'b0);
  ExactlyOne xor_7 (.out(xor_1_out[6]), .in0(or_6_out), .in2(1'b1), .in4(1'b0));
  and and_22 (and_22_out, or_7_out, 1'b0);
  and and_23 (and_23_out, or_7_out, 1'b0);
  and and_24 (and_24_out, 1'b0, 1'b0);
  ExactlyOne xor_8 (.out(xor_1_out[7]), .in0(or_7_out), .in2(1'b0), .in4(1'b0));
  or or_1 (or_1_out, and_1_out, and_2_out, and_3_out);
  or or_2 (or_2_out, and_4_out, and_5_out, and_6_out);
  or or_3 (or_3_out, and_7_out, and_8_out, and_9_out);
  or or_4 (or_4_out, and_10_out, and_11_out, and_12_out);
  or or_5 (or_5_out, and_13_out, and_14_out, and_15_out);
  or or_6 (or_6_out, and_16_out, and_17_out, and_18_out);
  or or_7 (or_7_out, and_19_out, and_20_out, and_21_out);
  or or_8 (or_8_out, and_22_out, and_23_out, and_24_out);
  // Probe on xor_1_out
endmodule
