// Logisim project alu1.circ as structural Verilog: 1 circuit, main circuit main
module main (
);

  wire and_17_out, and_18_out, and_19_out, and_20_out, and_21_out, and_22_out, and_23_out, and_24_out,
       and_25_out, and_26_out, and_27_out, and_28_out, and_29_out, and_30_out, and_31_out, and_32_out,
       and_33_out, and_34_out, and_35_out, and_36_out, and_37_out, and_38_out, and_39_out, and_40_out,
       and_41_out, and_42_out, and_43_out, and_44_out, and_45_out, and_46_out, and_47_out, and_48_out,
       and_49_out, and_50_out, and_51_out, and_52_out, and_53_out, and_54_out, and_55_out, and_56_out,
       and_57_out, and_58_out, and_59_out, and_60_out, and_61_out, and_62_out, and_63_out, and_64_out,
       and_65_out, nor_1_out, not_1_out, or_2_out, or_3_out, or_4_out, or_5_out, or_6_out, or_7_out,
       or_8_out, or_9_out, or_10_out, or_11_out, or_12_out, or_13_out, or_14_out, or_15_out, or_16_out,
       or_17_out, or_18_out, or_19_out, or_20_out, or_21_out, or_22_out;
  wire [15:0] or_1_out, xor_1_out, xor_17_out;
  wire [15:15] and_15_out;

  and and_1 (or_1_out[15], 1'b0, not_1_out);
  and and_2 (or_1_out[14], 1'b0, not_1_out);
  and and_3 (or_1_out[13], 1'b0, not_1_out);
  and and_4 (or_1_out[12], 1'b0, not_1_out);
  // Probe on nor_1_out
  // Probe on xor_17_out[15]
  and and_5 (or_1_out[10], 1'b0, not_1_out);
  and and_6 (or_1_out[11], 1'b0, not_1_out);
  // Probe on xor_17_out
  // Probe on {16{1'b0}}
  // Probe on {and_15_out[15], {15{1'b0}}}
  and and_7 (or_1_out[9], 1'b0, not_1_out);
  and and_8 (or_1_out[8], 1'b0, not_1_out);
  // Probe on or_22_out
  and and_9 (or_1_out[7], 1'b0, not_1_out);
  and and_10 (or_1_out[6], 1'b0, not_1_out);
  and and_11 (or_1_out[5], 1'b0, not_1_out);
  and and_12 (or_1_out[4], 1'b0, not_1_out);
  and and_13 (or_1_out[2], 1'b0, not_1_out);
  and and_14 (or_1_out[3], 1'b0, not_1_out);
  xor xor_1 (xor_1_out[0], or_1_out[0], or_3_out);
  xor xor_2 (xor_1_out[1], or_1_out[1], or_3_out);
  xor xor_3 (xor_1_out[2], or_1_out[2], or_3_out);
  xor xor_4 (xor_1_out[3], or_1_out[3], or_3_out);
  xor xor_5 (xor_1_out[4], or_1_out[4], or_3_out);
  xor xor_6 (xor_1_out[5], or_1_out[5], or_3_out);
  xor xor_7 (xor_1_out[6], or_1_out[6], or_3_out);
  xor xor_8 (xor_1_out[7], or_1_out[7], or_3_out);
  xor xor_9 (xor_1_out[8], or_1_out[8], or_3_out);
  xor xor_10 (xor_1_out[9], or_1_out[9], or_3_out);
  xor xor_11 (xor_1_out[10], or_1_out[10], or_3_out);
  xor xor_12 (xor_1_out[11], or_1_out[11], or_3_out);
  xor xor_13 (xor_1_out[12], or_1_out[12], or_3_out);
  xor xor_14 (xor_1_out[13], or_1_out[13], or_3_out);
  xor xor_15 (xor_1_out[14], or_1_out[14], or_3_out);
  xor xor_16 (xor_1_out[15], or_1_out[15], or_3_out);
  and and_15 (and_15_out[15], 1'b0, 1'b0);
  not not_1 (not_1_out, or_2_out);
  and and_16 (or_1_out[1], 1'b0, not_1_out);
  and and_17 (and_17_out, 1'b0, not_1_out);
  or or_1 (or_1_out[0], and_17_out, or_6_out);
  or or_2 (or_2_out, 1'b0, or_6_out);
  or or_3 (or_3_out, 1'b0, 1'b0);
  and and_18 (and_18_out, or_3_out, xor_1_out[0]);
  and and_19 (and_19_out, xor_1_out[0], 1'b0);
  and and_20 (and_20_out, 1'b0, or_3_out);
  ExactlyOne xor_17 (.out(xor_17_out[0]), .in0(or_3_out), .in1(xor_1_out[0]), .in2(1'b0));
  and and_21 (and_21_out, or_7_out, xor_1_out[1]);
  and and_22 (and_22_out, xor_1_out[1], 1'b0);
  and and_23 (and_23_out, 1'b0, or_7_out);
  ExactlyOne xor_18 (.out(xor_17_out[1]), .in0(or_7_out), .in1(xor_1_out[1]), .in2(1'b0));
  and and_24 (and_24_out, or_8_out, xor_1_out[2]);
  and and_25 (and_25_out, xor_1_out[2], 1'b0);
  and and_26 (and_26_out, 1'b0, or_8_out);
  ExactlyOne xor_19 (.out(xor_17_out[2]), .in0(or_8_out), .in1(xor_1_out[2]), .in2(1'b0));
  and and_27 (and_27_out, or_9_out, xor_1_out[3]);
  and and_28 (and_28_out, xor_1_out[3], 1'b0);
  and and_29 (and_29_out, 1'b0, or_9_out);
  ExactlyOne xor_20 (.out(xor_17_out[3]), .in0(or_9_out), .in1(xor_1_out[3]), .in2(1'b0));
  or or_4 (or_4_out, xor_17_out[0], xor_17_out[1], xor_17_out[2], xor_17_out[3], xor_17_out[4], xor_17_out[5], xor_17_out[6], xor_17_out[7], xor_17_out[8]);
  nor nor_1 (nor_1_out, or_4_out, or_5_out);
  or or_5 (or_5_out, xor_17_out[9], xor_17_out[10], xor_17_out[11], xor_17_out[12], xor_17_out[13], xor_17_out[14], xor_17_out[15]);
  or or_6 (or_6_out, 1'b0, 1'b0);
  or or_7 (or_7_out, and_18_out, and_19_out, and_20_out);
  or or_8 (or_8_out, and_21_out, and_22_out, and_23_out);
  or or_9 (or_9_out, and_24_out, and_25_out, and_26_out);
  or or_10 (or_10_out, and_27_out, and_28_out, and_29_out);
  and and_30 (and_30_out, or_10_out, xor_1_out[4]);
  and and_31 (and_31_out, xor_1_out[4], 1'b0);
  and and_32 (and_32_out, 1'b0, or_10_out);
  ExactlyOne xor_21 (.out(xor_17_out[4]), .in0(or_10_out), .in1(xor_1_out[4]), .in2(1'b0));
  and and_33 (and_33_out, or_11_out, xor_1_out[5]);
  and and_34 (and_34_out, xor_1_out[5], 1'b0);
  and and_35 (and_35_out, 1'b0, or_11_out);
  ExactlyOne xor_22 (.out(xor_17_out[5]), .in0(or_11_out), .in1(xor_1_out[5]), .in2(1'b0));
  and and_36 (and_36_out, or_12_out, xor_1_out[6]);
  and and_37 (and_37_out, xor_1_out[6], 1'b0);
  and and_38 (and_38_out, 1'b0, or_12_out);
  ExactlyOne xor_23 (.out(xor_17_out[6]), .in0(or_12_out), .in1(xor_1_out[6]), .in2(1'b0));
  and and_39 (and_39_out, or_13_out, xor_1_out[7]);
  and and_40 (and_40_out, xor_1_out[7], 1'b0);
  and and_41 (and_41_out, 1'b0, or_13_out);
  ExactlyOne xor_24 (.out(xor_17_out[7]), .in0(or_13_out), .in1(xor_1_out[7]), .in2(1'b0));
  or or_11 (or_11_out, and_30_out, and_31_out, and_32_out);
  or or_12 (or_12_out, and_33_out, and_34_out, and_35_out);
  or or_13 (or_13_out, and_36_out, and_37_out, and_38_out);
  or or_14 (or_14_out, and_39_out, and_40_out, and_41_out);
  and and_42 (and_42_out, or_14_out, xor_1_out[8]);
  and and_43 (and_43_out, xor_1_out[8], 1'b0);
  and and_44 (and_44_out, 1'b0, or_14_out);
  ExactlyOne xor_25 (.out(xor_17_out[8]), .in0(or_14_out), .in1(xor_1_out[8]), .in2(1'b0));
  and and_45 (and_45_out, or_15_out, xor_1_out[9]);
  and and_46 (and_46_out, xor_1_out[9], 1'b0);
  and and_47 (and_47_out, 1'b0, or_15_out);
  ExactlyOne xor_26 (.out(xor_17_out[9]), .in0(or_15_out), .in1(xor_1_out[9]), .in2(1'b0));
  and and_48 (and_48_out, or_16_out, xor_1_out[10]);
  and and_49 (and_49_out, xor_1_out[10], 1'b0);
  and and_50 (and_50_out, 1'b0, or_16_out);
  ExactlyOne xor_27 (.out(xor_17_out[10]), .in0(or_16_out), .in1(xor_1_out[10]), .in2(1'b0));
  and and_51 (and_51_out, or_17_out, xor_1_out[11]);
  and and_52 (and_52_out, xor_1_out[11], 1'b0);
  and and_53 (and_53_out, 1'b0, or_17_out);
  ExactlyOne xor_28 (.out(xor_17_out[11]), .in0(or_17_out), .in1(xor_1_out[11]), .in2(1'b0));
  or or_15 (or_15_out, and_42_out, and_43_out, and_44_out);
  or or_16 (or_16_out, and_45_out, and_46_out, and_47_out);
  or or_17 (or_17_out, and_48_out, and_49_out, and_50_out);
  or or_18 (or_18_out, and_51_out, and_52_out, and_53_out);
  and and_54 (and_54_out, or_18_out, xor_1_out[12]);
  and and_55 (and_55_out, xor_1_out[12], 1'b0);
  and and_56 (and_56_out, 1'b0, or_18_out);
  and and_57 (and_57_out, or_19_out, xor_1_out[13]);
  and and_58 (and_58_out, xor_1_out[13], 1'b0);
  and and_59 (and_59_out, 1'b0, or_19_out);
  and and_60 (and_60_out, or_20_out, xor_1_out[14]);
  and and_61 (and_61_out, xor_1_out[14], 1'b0);
  and and_62 (and_62_out, 1'b0, or_20_out);
  and and_63 (and_63_out, or_21_out, xor_1_out[15]);
  and and_64 (and_64_out, xor_1_out[15], 1'b0);
  and and_65 (and_65_out, 1'b0, or_21_out);
  or or_19 (or_19_out, and_54_out, and_55_out, and_56_out);
  ExactlyOne xor_29 (.out(xor_17_out[12]), .in0(or_18_out), .in1(xor_1_out[12]), .in2(1'b0));
  or or_20 (or_20_out, and_57_out, and_58_out, and_59_out);
  ExactlyOne xor_30 (.out(xor_17_out[13]), .in0(or_19_out), .in1(xor_1_out[13]), .in2(1'b0));
  or or_21 (or_21_out, and_60_out, and_61_out, and_62_out);
  ExactlyOne xor_31 (.out(xor_17_out[14]), .in0(or_20_out), .in1(xor_1_out[14]), .in2(1'b0));
  or or_22 (or_22_out, and_63_out, and_64_out, and_65_out);
  ExactlyOne xor_32 (.out(xor_17_out[15]), .in0(or_21_out), .in1(xor_1_out[15]), .in2(1'b0));

  // Notes on the sheet:
  //   These three values are multiplexed
  //   and then are routed to the Z
  //   register
  //   Sum
  //   S = 0
  //   S = Neg
  //   Left Shift Result
  //   Right Shift Result
  //   Carry-out
  //   Input B (from Y register)
  //   B = 0
  //   Left Shift
  //   Arith/Logical Right Shift
  //   B = 1
  //   Input A (from bus)
  //   Subtract
  //   Decrement
  //   Arithmetic Right Shift
  //   Increment
endmodule
