// Logisim project cu1.circ as structural Verilog: 1 circuit, main circuit main
module main (
);

  wire and_1_out, and_2_out, and_3_out, and_4_out, and_5_out, and_6_out, and_7_out, and_8_out, and_9_out,
       and_10_out, and_11_out, and_12_out, and_13_out, and_14_out, and_15_out, and_16_out, and_17_out,
       and_18_out, and_19_out, and_20_out, and_21_out, and_22_out, and_23_out, and_24_out, and_25_out,
       and_26_out, and_27_out, and_28_out, and_29_out, and_30_out, and_31_out, and_32_out, and_33_out,
       and_34_out, and_35_out, and_36_out, and_37_out, and_38_out, and_39_out, and_40_out, and_41_out,
       and_42_out, and_43_out, and_44_out, and_45_out, and_46_out, and_47_out, and_48_out, and_49_out,
       and_50_out, and_51_out, and_52_out, and_53_out, and_54_out, and_55_out, and_56_out, and_57_out,
       nor_1_out, not_1_out, not_2_out, not_3_out, not_4_out, not_5_out, not_6_out, not_7_out, not_8_out,
       or_1_out, or_2_out, or_3_out, or_4_out, or_5_out, or_6_out, or_7_out, or_8_out, or_9_out, or_10_out,
       or_11_out, or_12_out, or_13_out, or_14_out, or_15_out, or_16_out, or_17_out, or_18_out, or_19_out,
       or_20_out, or_21_out, or_22_out, or_23_out, or_24_out, or_25_out, or_26_out, or_27_out, or_28_out,
       or_29_out, or_30_out, or_31_out, or_32_out, or_33_out, or_34_out, or_35_out, or_36_out, or_37_out,
       or_38_out, or_39_out, or_40_out, or_41_out, or_42_out, or_43_out, or_44_out, or_45_out, or_46_out,
       or_47_out, or_48_out, or_49_out, or_50_out, or_51_out, or_52_out, or_53_out, undriven, undriven_2,
       undriven_3, undriven_4, undriven_5, undriven_6, undriven_7, undriven_8, undriven_9, undriven_10,
       undriven_11, undriven_12, undriven_13, undriven_14, undriven_15, undriven_16, undriven_17,
       undriven_18, undriven_19, undriven_20, undriven_21, undriven_22, undriven_23, undriven_24,
       undriven_25, undriven_26, undriven_27, undriven_28, undriven_29, undriven_30, undriven_31,
       undriven_32, undriven_33, undriven_34, undriven_35, undriven_36, undriven_37, undriven_38,
       undriven_39, undriven_40, undriven_41, undriven_42, undriven_43, undriven_44, undriven_45,
       undriven_46, undriven_47, undriven_48, undriven_49, undriven_50, undriven_51, undriven_52,
       undriven_53, undriven_54, undriven_55, undriven_56, undriven_57, undriven_58, undriven_59,
       undriven_60, undriven_61, undriven_62, undriven_63, undriven_64, undriven_65, undriven_66,
       undriven_67, undriven_68, undriven_69, undriven_70, undriven_71, undriven_72, undriven_73,
       undriven_74, undriven_75, undriven_76, undriven_77, undriven_78, undriven_79, undriven_80,
       undriven_81, undriven_82, undriven_83, undriven_84, undriven_85, undriven_86, undriven_87,
       undriven_88, undriven_89, undriven_90, undriven_91, undriven_92, undriven_93, undriven_94,
       undriven_95, undriven_96, undriven_97, undriven_98, undriven_99, undriven_100, undriven_101,
       undriven_102, undriven_103, undriven_104, undriven_105, undriven_106, undriven_107, undriven_108,
       undriven_109, undriven_110, undriven_111, undriven_112, undriven_113, undriven_114, undriven_115,
       undriven_116, undriven_117;

  // Probe on or_1_out
  // Probe on or_2_out
  // Probe on or_3_out
  // Probe on or_4_out
  // Probe on or_5_out
  // Probe on or_6_out
  // Probe on or_7_out
  // Probe on or_8_out
  // Probe on or_9_out
  // Probe on or_10_out
  // Probe on or_11_out
  // Probe on or_12_out
  // Probe on undriven
  // Probe on or_13_out
  // Probe on undriven_2
  // Probe on undriven_3
  // Probe on undriven_22
  // Probe on undriven_35
  // Probe on undriven_23
  // Probe on and_1_out
  // Probe on or_14_out
  // Probe on undriven_41
  // Probe on undriven_31
  or or_1 (or_1_out, undriven_4, undriven_5, undriven_7);
  or or_2 (or_2_out, undriven_6, undriven_39, undriven_41);
  or or_3 (or_3_out, undriven_7, undriven_8, undriven_9, undriven_10, undriven_11, undriven_12, undriven_13, undriven_14, undriven_15);
  or or_4 (or_4_out, undriven_16, undriven_17, undriven_18, undriven_19);
  or or_5 (or_5_out, undriven_41, undriven_20, undriven_21, undriven_45, undriven_3, undriven_22, undriven_35, undriven_23);
  or or_6 (or_6_out, undriven_5, undriven_42);
  or or_7 (or_7_out, undriven_24, undriven_25, undriven_2, undriven_6);
  or or_8 (or_8_out, undriven_26, undriven_37, undriven_29, undriven_20, undriven, undriven_27, undriven_28, undriven_4);
  or or_9 (or_9_out, undriven_10, undriven_55);
  or or_10 (or_10_out, undriven_43, undriven_47);
  or or_11 (or_11_out, undriven_29, undriven_30);
  or or_12 (or_12_out, undriven_47, undriven_24, undriven_31);
  or or_13 (or_13_out, undriven_27, undriven_28);
  // Probe on 1'b0
  and and_1 (and_1_out, undriven_42, undriven_32);
  and and_2 (and_2_out, undriven_36, undriven_42);
  or or_14 (or_14_out, and_2_out, undriven_55);
  and and_3 (and_3_out, undriven_38, undriven_33);
  // Probe on and_3_out
  // Probe on and_4_out
  and and_4 (and_4_out, undriven_38, undriven_77);
  and and_5 (and_5_out, undriven_38, undriven_34);
  // Probe on and_5_out
  // Probe on or_15_out
  or or_15 (or_15_out, undriven_10, undriven_37, undriven_38);
  // Probe on 1'b0
  // Probe on or_16_out
  or or_16 (or_16_out, undriven_39, undriven_43, undriven_37, undriven_40);
  // Probe on or_17_out
  or or_17 (or_17_out, undriven_47, undriven_41, undriven_31, undriven_42, undriven_38);
  not not_1 (not_1_out, 1'b1);
  // Probe on or_18_out
  // Probe on or_19_out
  or or_18 (or_18_out, undriven_42, undriven_47, undriven_31, undriven_41, undriven_38);
  or or_19 (or_19_out, undriven_30, undriven_40, undriven_43, undriven_7, undriven_45);
  // Probe on or_20_out
  // Probe on undriven_26
  or or_20 (or_20_out, undriven_55, undriven_45);
  or or_21 (or_21_out, undriven_48, and_6_out);
  and and_6 (and_6_out, undriven_49, not_1_out);
  or or_22 (or_22_out, undriven_50, and_7_out);
  and and_7 (and_7_out, undriven_51, not_1_out);
  or or_23 (or_23_out, undriven_44, and_8_out);
  and and_8 (and_8_out, undriven_52, not_1_out);
  or or_24 (or_24_out, undriven_46, and_9_out);
  and and_9 (and_9_out, undriven_54, not_1_out);
  and and_10 (and_10_out, 1'b1, undriven_49);
  and and_11 (and_11_out, 1'b1, undriven_51);
  and and_12 (and_12_out, 1'b1, undriven_52);
  and and_13 (and_13_out, 1'b1, undriven_54);
  not not_2 (not_2_out, 1'b0);
  and and_14 (and_14_out, not_7_out, not_2_out, or_25_out);
  or or_25 (or_25_out, undriven_78, undriven_79, undriven_59, undriven_66, undriven_80, undriven_76, and_17_out, and_15_out, or_26_out);
  or or_26 (or_26_out, undriven_82, and_16_out);
  and and_15 (and_15_out, undriven_81, 1'b1);
  and and_16 (and_16_out, undriven_63, 1'b1);
  and and_17 (and_17_out, or_34_out, or_28_out);
  or or_27 (or_27_out, 1'b0, 1'b0);
  not not_3 (not_3_out, 1'b0);
  or or_28 (or_28_out, undriven_86, undriven_89, undriven_87);
  and and_18 (and_18_out, undriven_58, or_29_out);
  or or_29 (or_29_out, 1'b0, not_4_out);
  not not_4 (not_4_out, or_38_out);
  or or_30 (or_30_out, undriven_92, undriven_95);
  not not_5 (not_5_out, 1'b1);
  and and_19 (and_19_out, 1'b1, undriven_57);
  not not_6 (not_6_out, or_27_out);
  or or_31 (or_31_out, undriven_56, and_20_out);
  and and_20 (and_20_out, not_5_out, undriven_57);
  or or_32 (or_32_out, undriven_61, and_21_out);
  and and_21 (and_21_out, not_5_out, undriven_97);
  or or_33 (or_33_out, undriven_62, and_22_out);
  and and_22 (and_22_out, not_5_out, undriven_63);
  or or_34 (or_34_out, undriven_91, and_23_out);
  and and_23 (and_23_out, not_5_out, undriven_68);
  and and_24 (and_24_out, undriven_68, 1'b1);
  and and_25 (and_25_out, not_5_out, undriven_81);
  or or_35 (or_35_out, undriven_73, and_26_out);
  and and_26 (and_26_out, not_5_out, undriven_58);
  and and_27 (and_27_out, undriven_58, 1'b1);
  or or_36 (or_36_out, undriven_74, and_28_out);
  and and_28 (and_28_out, not_5_out, undriven_75);
  and and_29 (and_29_out, undriven_75, 1'b1);
  or or_37 (or_37_out, undriven_94, undriven_102, undriven_83, undriven_84, undriven_104, undriven_105, undriven_85, undriven_93, or_38_out);
  or or_38 (or_38_out, undriven_88, undriven_90);
  and and_30 (and_30_out, and_18_out, or_39_out);
  or or_39 (or_39_out, or_30_out, and_31_out);
  or or_40 (or_40_out, and_32_out, and_36_out);
  and and_31 (and_31_out, or_37_out, not_6_out);
  and and_32 (and_32_out, or_34_out, or_28_out);
  and and_33 (and_33_out, and_18_out, or_28_out);
  or or_41 (or_41_out, undriven_60, undriven_64);
  or or_42 (or_42_out, undriven_72, and_25_out);
  and and_34 (and_34_out, undriven_69, undriven_92, or_28_out);
  and and_35 (and_35_out, not_3_out, or_41_out);
  or or_43 (or_43_out, and_35_out, and_34_out);
  not not_7 (not_7_out, nor_1_out);
  and and_36 (and_36_out, and_18_out, or_44_out);
  or or_44 (or_44_out, and_37_out, or_30_out);
  and and_37 (and_37_out, or_27_out, or_37_out);
  and and_38 (and_38_out, or_41_out, 1'b0);
  and and_39 (and_39_out, or_43_out, undriven_95);
  and and_40 (and_40_out, and_18_out, undriven_92);
  or or_45 (or_45_out, undriven_83, undriven_84);
  or or_46 (or_46_out, nor_1_out, 1'b0);
  and and_41 (and_41_out, or_46_out, or_25_out);
  and and_42 (and_42_out, or_43_out, undriven_94);
  and and_43 (and_43_out, or_43_out, undriven_102);
  and and_44 (and_44_out, or_27_out, undriven_97);
  and and_45 (and_45_out, or_43_out, undriven_93);
  and and_46 (and_46_out, or_43_out, undriven_96);
  not not_8 (not_8_out, not_5_out);
  and and_47 (and_47_out, undriven_88, or_43_out);
  and and_48 (and_48_out, undriven_90, or_43_out);
  or or_47 (or_47_out, undriven_99, undriven_100, undriven_101, undriven_103, undriven_106, undriven_107, undriven_108, undriven_109);
  nor nor_1 (nor_1_out, or_47_out, or_52_out);
  or or_48 (or_48_out, undriven_53, and_41_out);
  and and_49 (and_49_out, or_43_out, or_45_out);
  and and_50 (and_50_out, undriven_65, not_5_out);
  and and_51 (and_51_out, undriven_65, 1'b1);
  or or_49 (or_49_out, and_52_out, undriven_70);
  and and_52 (and_52_out, not_5_out, undriven_71);
  and and_53 (and_53_out, undriven_71, not_8_out);
  or or_50 (or_50_out, undriven_67, and_54_out, and_55_out);
  and and_54 (and_54_out, or_43_out, or_51_out);
  and and_55 (and_55_out, undriven_69, undriven_92, or_28_out);
  or or_51 (or_51_out, undriven_104, and_57_out, and_56_out);
  and and_56 (and_56_out, undriven_85, 1'b0);
  and and_57 (and_57_out, undriven_105, or_28_out);
  or or_52 (or_52_out, undriven_110, undriven_111, undriven_112, undriven_113, undriven_114, undriven_115, undriven_116, undriven_117);
  or or_53 (or_53_out, and_50_out, undriven_98);
  // also tied to GND on the sheet: or_28_out

  // Notes on the sheet:
  //   PC_in
  //   PC_out
  //   READ_MM
  //   WRITE_MM
  //   MAR_in
  //   MAR_out
  //   MDR_in
  //   MDR_out
  //   IDX_in
  //   IDX_out
  //   Timer_in
  //   PSW_in
  //   PSW_out
  //   ROM(4)_out
  //   ROM(5)_out
  //   ROM(6)_out
  //   ROM(7)_out
  //   ALU_subtract
  //   ALU_decrement
  //   ALU_rightshift(arithmetic)
  //   Y_in
  //   Y_out
  //   Index Register Control Bits I0,I1
  //   ALU_add
  //   ALU_inc
  //   ALU_rightshift(logical)
  //   ALU_leftshift
  //   ACC_out
  //   ACC_in
  //   Z_out
  //   ALU_busin
  //   Z_in
  //   INTR1
  //   INTR2
  //   INTR3
  //   INTR4
  //   INTR5
  //   INTR6
  //   INTR7
  //   INTR8
  //   INTR9
  //   INTR10
  //   INTR11
  //   INTR12
  //   INTR13
  //   INTR14
  //   INTR15
  //   INTR16
  //   IR.address_out
  //   Flip-Flop Outputs 39-54 (Current State)
  //   IR_in
  //   <-- WMFC
  //   This is true when it's time to go to interrupt state-->
  //   Flip-Flop Outputs 0-9 (Current State)
  //   F1
  //   F2
  //   F3
  //   F4
  //   SH1
  //   SH2
  //   EA1
  //   EA2
  //   LDA1
  //   LDA2
  //   Flip-Flop Outputs 10-19 (Current State)
  //   LDA3
  //   STA1
  //   STA2
  //   STA3
  //   EA3
  //   EA4
  //   ADD1
  //   ADD2
  //   ADD3
  //   ADD4
  //   Flip-Flop Outputs 20-29 (Current State)
  //   BRU1
  //   JSR1
  //   EA5
  //   EA6
  //   EA7
  //   LDX1
  //   LDX2
  //   LDX3
  //   STX1
  //   STX2
  //   Flip-Flop Outputs 30-38 (Current State)
  //   STX3
  //   TDX1
  //   TDX2
  //   CLK1
  //   CLK2
  //   CLK3
  //   LPSW1
  //   LPSW2
  //   LPSW3
  //   Flip-Flop Inputs 39-54 (Next State)
  //   INTR1
  //   INTR2
  //   INTR3
  //   INTR4
  //   INTR5
  //   INTR6
  //   INTR7
  //   INTR8
  //   INTR9
  //   INTR10
  //   INTR11
  //   INTR12
  //   INTR13
  //   INTR14
  //   INTR15
  //   INTR16
  //   IDX offset, bit 0
  //   IDX offset, bit 1
  //   Indirect
  //   W
  //   OPCODE->Decoder
  //   Shift Operation -->
  //   LDA
  //   STA
  //   ADD
  //   SUB
  //   BRU
  //   BIZ
  //   BIN
  //   JSR
  //   SHRA
  //   SHR
  //   SHL
  //   LDX
  //   STX
  //   TDX
  //   CLK
  //   LPSW
  //   PSW.P
  //   PSW.N
  //   P
  //   PSW.Z
  //   WMFC
  //   <-- EA must be calc
  //   without IDX offset
  //   Priveliged Op
  //   X
  //   Require EA calculation
  //   Countdown Timer value
  //   <-- Add/Subtract Op
  //   Countdown timer > 0
  //   Flip-Flop Inputs 0-9 (Next State)
  //   F1
  //   F2
  //   F3
  //   F4
  //   SH1
  //   SH2
  //   EA1
  //   EA2
  //   LDA1
  //   LDA2
  //   Flip-Flop Inputs 10-19 (Next State)
  //   LDA3
  //   STA1
  //   STA2
  //   STA3
  //   EA3
  //   EA4
  //   ADD1
  //   ADD2
  //   ADD3
  //   ADD4
  //   Flip-Flop Inputs 20-29 (Next State)
  //   BRU1
  //   JSR1
  //   EA5
  //   EA6
  //   EA7
  //   LDX1
  //   LDX2
  //   LDX3
  //   STX1
  //   STX2
  //   Flip-Flop Inputs 30-38 (Next State)
  //   STX3
  //   TDX1
  //   TDX2
  //   CLK1
  //   CLK2
  //   CLK3
  //   LPSW1
  //   LPSW2
  //   LPSW3
endmodule
