// Logisim project mirco-sequencer1.circ as structural Verilog: 1 circuit, main circuit main
module main (
);

  wire and_1_out, and_2_out, and_3_out, and_4_out, and_5_out, and_6_out, and_7_out, and_8_out, and_9_out,
       and_10_out, and_11_out, and_12_out, and_13_out, and_14_out, and_15_out, and_16_out, and_17_out,
       and_18_out, and_19_out, and_20_out, and_21_out, and_22_out, and_23_out, and_24_out, and_25_out,
       and_26_out, nand_1_out, nor_1_out, not_1_out, not_2_out, or_1_out, or_2_out, or_3_out, or_4_out,
       or_5_out, or_6_out, or_7_out, or_8_out, or_9_out, or_10_out, or_11_out, or_12_out, or_13_out,
       or_14_out, or_15_out, undriven, undriven_2, undriven_3, undriven_4, undriven_5, undriven_6,
       undriven_7, undriven_8, undriven_9, undriven_10, undriven_11, undriven_12, undriven_13, undriven_14,
       undriven_15, undriven_16, undriven_17, undriven_18, undriven_19, undriven_20, undriven_21,
       undriven_22, undriven_23, undriven_24, undriven_25, undriven_26, undriven_27, undriven_28,
       undriven_29, undriven_30, undriven_31, undriven_32, undriven_33, undriven_34, undriven_35,
       undriven_36, undriven_37, undriven_38, undriven_39;

  and and_1 (and_1_out, nand_1_out, undriven);
  and and_2 (and_2_out, nand_1_out, undriven_2);
  and and_3 (and_3_out, nand_1_out, undriven_3);
  and and_4 (and_4_out, undriven_38, or_2_out);
  or or_1 (or_1_out, undriven_5, undriven_2);
  or or_2 (or_2_out, undriven_6, undriven);
  and and_5 (and_5_out, undriven_38, or_1_out);
  and and_6 (and_6_out, undriven_38, or_3_out);
  or or_3 (or_3_out, undriven_4, undriven_3);
  or or_4 (or_4_out, undriven_8, undriven_9, undriven);
  and and_7 (and_7_out, undriven_7, or_4_out);
  and and_8 (and_8_out, undriven_7, or_7_out);
  or or_5 (or_5_out, and_2_out, and_5_out, and_8_out);
  or or_6 (or_6_out, and_1_out, and_4_out, and_7_out);
  or or_7 (or_7_out, undriven_10, undriven_2);
  or or_8 (or_8_out, undriven_11, undriven_3);
  and and_9 (and_9_out, undriven_7, or_8_out);
  or or_9 (or_9_out, and_3_out, and_6_out, and_9_out);
  nand nand_1 (nand_1_out, undriven_38, undriven_7);
  or or_10 (or_10_out, undriven_28, undriven_29);
  or or_11 (or_11_out, undriven_39, undriven_31);
  and and_10 (and_10_out, undriven_37, or_11_out);
  and and_11 (and_11_out, undriven_36, undriven_12);
  or or_12 (or_12_out, undriven_7, and_10_out, undriven_38, undriven_30, undriven_35);
  and and_12 (and_12_out, undriven_36, undriven_14);
  and and_13 (and_13_out, undriven_36, undriven_13);
  and and_14 (and_14_out, undriven_36, undriven_15);
  and and_15 (and_15_out, undriven_36, undriven_16);
  and and_16 (and_16_out, undriven_36, undriven_17);
  and and_17 (and_17_out, undriven_36, undriven_18);
  and and_18 (and_18_out, undriven_36, undriven_19);
  and and_19 (and_19_out, undriven_36, undriven_20);
  and and_20 (and_20_out, undriven_36, undriven_21);
  and and_21 (and_21_out, undriven_36, undriven_22);
  and and_22 (and_22_out, undriven_36, undriven_23);
  and and_23 (and_23_out, undriven_36, undriven_24);
  and and_24 (and_24_out, undriven_36, undriven_26);
  and and_25 (and_25_out, undriven_36, undriven_25);
  and and_26 (and_26_out, undriven_36, undriven_27);
  not not_1 (not_1_out, undriven_32);
  not not_2 (not_2_out, undriven_33);
  or or_13 (or_13_out, not_2_out, not_1_out, undriven_34, or_10_out, and_26_out, and_24_out, and_25_out, and_23_out, and_22_out);
  nor nor_1 (nor_1_out, or_13_out, or_14_out, or_15_out, undriven_30);
  or or_14 (or_14_out, and_21_out, and_20_out, and_19_out);
  or or_15 (or_15_out, and_18_out, and_17_out, and_16_out, and_15_out, and_14_out, and_12_out, and_13_out, and_11_out, or_12_out);

  // Notes on the sheet:
  //   fetch
  //   indexing
  //   indirect
  //   trap
  //   reset
  //   X_lda
  //   X_sta
  //   X_add
  //   X_sub
  //   X_bru
  //   X_biz
  //   X_bin
  //   X_jsr
  //   X_shra
  //   X_shr
  //   X_shl
  //   X_ldx
  //   X_stx
  //   X_tdx
  //   X_clk
  //   X_lpsw
  //   address constants
  //   logical ACC
  //   high ACC
  //   logical IDX
  //   IR 0-3
  //   addr bit0
  //   specified branch-to-address
  //   modified address
  //   indirect bit
  //   opcode (decoded)
  //   LDA
  //   STA
  //   ADD
  //   SUB
  //   BRU
  //   BIZ
  //   BIN
  //   JSR
  //   SHRA
  //   SHR
  //   SHL
  //   LDX
  //   STX
  //   TDX
  //   CLK
  //   LPSW
  //   effective address bits
  //   index bit0
  //   index bit1
  //   processor status word
  //   zero
  //   neg
  //   priv
  //   main memory signals
  //   MFC
  //   countdown timer
  //   timer > 0
  //   branching
  //   j
  //   j_opcode
  //   j_psw
  //   j_ii
  //   j_reg
  //   addr bit31
  //   GOTO:
  //   specified address
  //   might be modified
  //   due to j_reg or j_ii
  //   X_lda
  //   microinstruction
  //   X_add
  //   X_sta
  //   X_sub
  //   X_bru
  //   X_bin
  //   X_biz
  //   X_jsr
  //   X_shra
  //   X_shl
  //   X_shr
  //   X_stx
  //   X_ldx
  //   X_tdx
  //   X_clk
  //   X_lpsw
  //   indexing
  //   reset
  //   trap
  //   stay at current
  //   indirect
  //   next address
endmodule
