// Logisim project reg.circ as structural Verilog: 1 circuit, main circuit main
module main (
);

  wire and_1_out, and_2_out, and_3_out, and_4_out, and_5_out, and_6_out, and_7_out, and_8_out, and_9_out,
       and_10_out, and_11_out, and_12_out, and_13_out, and_14_out, and_15_out, and_16_out, and_17_out,
       and_18_out, and_19_out, and_20_out, and_21_out, and_22_out, and_23_out, and_24_out, and_25_out,
       and_26_out, and_27_out, and_28_out, and_29_out, and_30_out, and_31_out, and_32_out, not_1_out,
       not_2_out, not_3_out, not_4_out, not_5_out, not_6_out, not_7_out, not_8_out, not_9_out, not_10_out,
       not_11_out, not_12_out, not_13_out, not_14_out, not_15_out, not_16_out, or_2_out, or_4_out, or_6_out,
       or_8_out, or_10_out, or_12_out, or_14_out, or_16_out, or_18_out, or_20_out, or_22_out, or_24_out,
       or_26_out, or_28_out, or_30_out, or_32_out;
  wire [15:0] or_1_out, undriven;

  and and_1 (and_1_out, undriven[0], 1'b1);
  and and_2 (and_2_out, 1'b1, not_1_out);
  not not_1 (not_1_out, undriven[0]);
  and and_3 (and_3_out, undriven[4], 1'b1);
  and and_4 (and_4_out, 1'b1, not_2_out);
  not not_2 (not_2_out, undriven[4]);
  and and_5 (and_5_out, undriven[8], 1'b1);
  and and_6 (and_6_out, 1'b1, not_3_out);
  not not_3 (not_3_out, undriven[8]);
  and and_7 (and_7_out, undriven[12], 1'b1);
  and and_8 (and_8_out, 1'b1, not_4_out);
  not not_4 (not_4_out, undriven[12]);
  or or_1 (or_1_out[0], and_1_out, or_2_out);
  or or_2 (or_2_out, or_1_out[0], and_2_out);
  not not_5 (not_5_out, undriven[1]);
  or or_3 (or_1_out[4], and_3_out, or_4_out);
  or or_4 (or_4_out, or_1_out[4], and_4_out);
  not not_6 (not_6_out, undriven[5]);
  or or_5 (or_1_out[8], and_5_out, or_6_out);
  or or_6 (or_6_out, or_1_out[8], and_6_out);
  not not_7 (not_7_out, undriven[9]);
  or or_7 (or_1_out[12], and_7_out, or_8_out);
  or or_8 (or_8_out, or_1_out[12], and_8_out);
  not not_8 (not_8_out, undriven[13]);
  and and_9 (and_9_out, undriven[1], 1'b1);
  or or_9 (or_1_out[1], and_9_out, or_10_out);
  or or_10 (or_10_out, or_1_out[1], and_10_out);
  and and_10 (and_10_out, 1'b1, not_5_out);
  and and_11 (and_11_out, undriven[5], 1'b1);
  or or_11 (or_1_out[5], and_11_out, or_12_out);
  or or_12 (or_12_out, or_1_out[5], and_12_out);
  and and_12 (and_12_out, 1'b1, not_6_out);
  and and_13 (and_13_out, undriven[9], 1'b1);
  or or_13 (or_1_out[9], and_13_out, or_14_out);
  or or_14 (or_14_out, or_1_out[9], and_14_out);
  and and_14 (and_14_out, 1'b1, not_7_out);
  and and_15 (and_15_out, undriven[13], 1'b1);
  or or_15 (or_1_out[13], and_15_out, or_16_out);
  or or_16 (or_16_out, or_1_out[13], and_16_out);
  and and_16 (and_16_out, 1'b1, not_8_out);
  not not_9 (not_9_out, undriven[2]);
  not not_10 (not_10_out, undriven[6]);
  not not_11 (not_11_out, undriven[10]);
  not not_12 (not_12_out, undriven[14]);
  and and_17 (and_17_out, undriven[2], 1'b1);
  or or_17 (or_1_out[2], and_17_out, or_18_out);
  or or_18 (or_18_out, or_1_out[2], and_18_out);
  and and_18 (and_18_out, 1'b1, not_9_out);
  and and_19 (and_19_out, undriven[6], 1'b1);
  or or_19 (or_1_out[6], and_19_out, or_20_out);
  or or_20 (or_20_out, or_1_out[6], and_20_out);
  and and_20 (and_20_out, 1'b1, not_10_out);
  and and_21 (and_21_out, undriven[10], 1'b1);
  or or_21 (or_1_out[10], and_21_out, or_22_out);
  or or_22 (or_22_out, or_1_out[10], and_22_out);
  and and_22 (and_22_out, 1'b1, not_11_out);
  and and_23 (and_23_out, undriven[14], 1'b1);
  or or_23 (or_1_out[14], and_23_out, or_24_out);
  or or_24 (or_24_out, or_1_out[14], and_24_out);
  and and_24 (and_24_out, 1'b1, not_12_out);
  and and_25 (and_25_out, undriven[3], 1'b1);
  and and_26 (and_26_out, 1'b1, not_13_out);
  not not_13 (not_13_out, undriven[3]);
  and and_27 (and_27_out, undriven[7], 1'b1);
  and and_28 (and_28_out, 1'b1, not_14_out);
  not not_14 (not_14_out, undriven[7]);
  and and_29 (and_29_out, undriven[11], 1'b1);
  and and_30 (and_30_out, 1'b1, not_15_out);
  not not_15 (not_15_out, undriven[11]);
  and and_31 (and_31_out, undriven[15], 1'b1);
  and and_32 (and_32_out, 1'b1, not_16_out);
  not not_16 (not_16_out, undriven[15]);
  or or_25 (or_1_out[3], and_25_out, or_26_out);
  or or_26 (or_26_out, or_1_out[3], and_26_out);
  or or_27 (or_1_out[7], and_27_out, or_28_out);
  or or_28 (or_28_out, or_1_out[7], and_28_out);
  or or_29 (or_1_out[11], and_29_out, or_30_out);
  or or_30 (or_30_out, or_1_out[11], and_30_out);
  or or_31 (or_1_out[15], and_31_out, or_32_out);
  or or_32 (or_32_out, or_1_out[15], and_32_out);

  // Notes on the sheet:
  //   Inputs (D)
  //   Enable
  //   Outputs (Q)
endmodule
